// Digital circuit decodeur64.dig as structural Verilog
module decodeur64 (
  input  [5:0] e,
  input  en,
  output _1,
  output _2,
  output _3,
  output _4,
  output _5,
  output _6,
  output _7,
  output _8,
  output _9,
  output _10,
  output _11,
  output _12,
  output _13,
  output _14,
  output _15,
  output _16,
  output _17,
  output _18,
  output _19,
  output _20,
  output _21,
  output _22,
  output _23,
  output _24,
  output _25,
  output _26,
  output _27,
  output _28,
  output _29,
  output _30,
  output _31,
  output _32,
  output _33,
  output _34,
  output _35,
  output _36,
  output _37,
  output _38,
  output _39,
  output _40,
  output _41,
  output _42,
  output _43,
  output _44,
  output _45,
  output _46,
  output _47,
  output _48,
  output _49,
  output _50,
  output _51,
  output _52,
  output _53,
  output _54,
  output _55,
  output _56,
  output _57,
  output _58,
  output _59,
  output _60,
  output _61,
  output _62,
  output _63,
  output _0
);

  wire decoder_1_out_0;
  wire [5:0] multiplexer_1_out;

  Multiplexer #(.Bits(6)) multiplexer_1 (.sel(en), .in_0({6{1'b0}}), .in_1(e), .out(multiplexer_1_out));
  Decoder #(.Selector_Bits(6)) decoder_1 (
    .sel(multiplexer_1_out), .out_0(decoder_1_out_0), .out_1(_1), .out_2(_2), .out_3(_3), .out_4(_4),
    .out_5(_5), .out_6(_6), .out_7(_7), .out_8(_8), .out_9(_9), .out_10(_10), .out_11(_11), .out_12(_12),
    .out_13(_13), .out_14(_14), .out_15(_15), .out_16(_16), .out_17(_17), .out_18(_18), .out_19(_19),
    .out_20(_20), .out_21(_21), .out_22(_22), .out_23(_23), .out_24(_24), .out_25(_25), .out_26(_26),
    .out_27(_27), .out_28(_28), .out_29(_29), .out_30(_30), .out_31(_31), .out_32(_32), .out_33(_33),
    .out_34(_34), .out_35(_35), .out_36(_36), .out_37(_37), .out_38(_38), .out_39(_39), .out_40(_40),
    .out_41(_41), .out_42(_42), .out_43(_43), .out_44(_44), .out_45(_45), .out_46(_46), .out_47(_47),
    .out_48(_48), .out_49(_49), .out_50(_50), .out_51(_51), .out_52(_52), .out_53(_53), .out_54(_54),
    .out_55(_55), .out_56(_56), .out_57(_57), .out_58(_58), .out_59(_59), .out_60(_60), .out_61(_61),
    .out_62(_62), .out_63(_63));
  and and_1 (_0, en, decoder_1_out_0);
endmodule

/* Test case Test:
          en   e	63 62  61 60 59 58 57 56 55 54 53 52 51 50 49 48 47 46 45 44 43 42 41 40 39 38 37 36 35 34 33 32 31 30 29 28 27 26 25 24 23 22 21 20 19 18 17 16 15 14 13 12 11 10 9 8 7 6 5 4 3 2 1 0         
repeat(32)0   (n)  bits(32,0)  bits(32,0)
repeat(32)1   (n)  bits(32,0)  bits(32,1<<n)   
repeat(32)0   (n+32)  bits(32,0)  bits(32,0)                
repeat(32)1   (n+32)  bits(32,1<<n)  bits(32,0)                   
*/
