// Digital circuit mips.dig as structural Verilog
module mips (
  input  C,
  output [31:0] cp,
  output [31:0] res
);

  wire and_1_out, and_2_out, and_3_out, and_4_out, and_5_out, and_6_out, and_7_out, beq, bgtz, blez, bne,
       cns, comparator_1_eq, comparator_2_eq, comparator_3_eq, comparator_4_eq, d_m, Data_p10, Data_p11,
       delay_1_out, eq_0, ereg, jal, jr, ld, lt_0, lt__eq_0, mem_8, mfhi, mflo, mx_1, mx_br, mx_shamt, Ns,
       or_1_out, str;
  wire [0:0] keyboard_1_av;
  wire [3:0] Op_ual;
  wire [4:0] multiplexer_2_out, multiplexer_6_out;
  wire [5:0] Co;
  wire [15:0] keyboard_1_d;
  wire [23:0] Data_p8, meminst_1_p4;
  wire [27:2] Imm26;
  wire [31:0] add_2_s, cp_plus_4, cp_q, Data_p7, Data_p9, data_read, HI, Imms, Imms_lt__lt_2, LO, mem_read,
       meminst_1_p2, multiplexer_1_out, multiplexer_3_out, multiplexer_4_out, multiplexer_5_out,
       multiplexer_7_out, multiplexer_8_out, multiplexer_9_out, multiplexer_10_out, multiplexer_12_out,
       multiplexer_13_out, multiplexer_14_out, multiplexer_16_out, ual0_1_hi, ual0_1_lo, val_rs, val_rt;

  Add #(.Bits(32)) add_1 (.a(cp), .b(32'h4), .c_i(1'b0), .s(cp_plus_4));  // open: c_o
  Add #(.Bits(32)) add_2 (.a(cp_plus_4), .b(Imms_lt__lt_2), .c_i(1'b0), .s(add_2_s));  // open: c_o
  Multiplexer #(.Bits(32)) multiplexer_1 (.sel(ld), .in_0(res), .in_1(data_read), .out(multiplexer_1_out));
  Multiplexer #(.Bits(5)) multiplexer_2 (.sel(mx_1), .in_0(Imm26[22:18]), .in_1(Imm26[17:13]), .out(multiplexer_2_out));
  Multiplexer #(.Bits(32)) multiplexer_3 (.sel(mx_br), .in_0(cp_plus_4), .in_1(add_2_s), .out(multiplexer_3_out));
  Multiplexer #(.Bits(32)) multiplexer_4 (.sel(mfhi), .in_0(multiplexer_1_out), .in_1(HI), .out(multiplexer_4_out));
  Comparator #(.Bits(32)) comparator_1 (.a(res), .b(32'hffff000c), .eq(comparator_1_eq));  // open: gt, lt
  Comparator #(.Bits(32)) comparator_2 (.a(res), .b(32'hffff0000), .eq(comparator_2_eq));  // open: gt, lt
  Comparator #(.Bits(32)) comparator_3 (.a(res), .b(32'hffff0004), .eq(comparator_3_eq));  // open: gt, lt
  Multiplexer #(.Bits(32)) multiplexer_5 (.sel(mflo), .in_0(multiplexer_4_out), .in_1(LO), .out(multiplexer_5_out));
  Multiplexer #(.Bits(5)) multiplexer_6 (
    .sel(jal), .in_0(multiplexer_2_out), .in_1({5{1'b0}}), .out(multiplexer_6_out));
  and and_1 (and_1_out, comparator_1_eq, str);
  and and_2 (and_2_out, comparator_2_eq, ld);
  and and_3 (and_3_out, comparator_3_eq, ld);
  Delay delay_1 (.in(C), .out(delay_1_out));
  Multiplexer #(.Bits(32)) multiplexer_7 (.sel(jr), .in_0(multiplexer_3_out), .in_1(val_rs), .out(multiplexer_7_out));
  Multiplexer #(.Bits(32)) multiplexer_8 (
    .sel(jal), .in_0(multiplexer_5_out), .in_1(cp_plus_4), .out(multiplexer_8_out));
  Multiplexer #(.Bits(32)) multiplexer_9 (
    .sel(jal), .in_0(multiplexer_7_out), .in_1({4'b0000, Imm26, 2'b00}), .out(multiplexer_9_out));
  RegisterFile #(.AddrBits(5), .Bits(32)) registerfile_1 (
    .Din(multiplexer_8_out), .we(ereg), .Rw(multiplexer_6_out), .C(delay_1_out), .Ra(Imm26[27:23]),
    .Rb(Imm26[22:18]), .Da(val_rs), .Db(val_rt));
  Keyboard keyboard_1 (.C(C), .en(and_3_out), .D(keyboard_1_d), .av(keyboard_1_av[0]));
  Register #(.Bits(32)) u_cp (.D(multiplexer_9_out), .C(~C), .en(1'b1), .Q(cp_q));
  Comparator #(.Bits(32)) comparator_4 (.a(cp_q), .b({32{1'b0}}), .eq(comparator_4_eq));  // open: gt, lt
  Multiplexer #(.Bits(32)) multiplexer_10 (
    .sel(and_3_out), .in_0(mem_read), .in_1({{16{1'b0}}, keyboard_1_d}), .out(multiplexer_10_out));
  Multiplexer #(.Bits(32)) multiplexer_11 (.sel(comparator_4_eq), .in_0(cp_q), .in_1(32'h400000), .out(cp));
  Multiplexer #(.Bits(32)) multiplexer_12 (
    .sel(mx_shamt), .in_0(val_rs), .in_1({{27{1'b0}}, Imm26[12:8]}), .out(multiplexer_12_out));
  Multiplexer #(.Bits(32)) multiplexer_13 (
    .sel(Ns), .in_0(Imms), .in_1({{16{1'b0}}, Imm26[17:2]}), .out(multiplexer_13_out));
  Multiplexer #(.Bits(32)) multiplexer_14 (
    .sel(mx_1), .in_0(multiplexer_13_out), .in_1(val_rt), .out(multiplexer_14_out));
  or or_1 (or_1_out, blez, bgtz);
  Multiplexer #(.Bits(32)) multiplexer_15 (
    .sel(and_2_out), .in_0(multiplexer_10_out), .in_1({{31{1'b0}}, keyboard_1_av[0]}), .out(data_read));
  Multiplexer #(.Bits(32)) multiplexer_16 (
    .sel(or_1_out), .in_0(multiplexer_14_out), .in_1({32{1'b0}}), .out(multiplexer_16_out));
  ual0 ual0_1 (
    .Op(Op_ual), .B(multiplexer_16_out), .A(multiplexer_12_out), .HI(ual0_1_hi), .LO(ual0_1_lo), .S(res),
    .lt__eq_0(lt__eq_0), .eq_0(eq_0), .lt_0(lt_0));
  Terminal terminal_1 (.D(val_rt), .C(C), .en(and_1_out));
  // memInst meminst_1: pin names not known; wires that end beside it: cp, meminst_1_p2, {Co, Imm26}, meminst_1_p4
  ROM #(.AddrBits(24), .Bits(32)) rom_1 (.A(meminst_1_p4), .sel(1'b1), .D(meminst_1_p2));
  Register #(.Bits(32)) u_HI (.D(ual0_1_hi), .C(C), .en(d_m), .Q(HI));
  Register #(.Bits(32)) u_LO (.D(ual0_1_lo), .C(C), .en(d_m), .Q(LO));
  // memData Data: pin names not known; wires that end beside it: res, val_rt, str, ld, mem_8, cns, Data_p7, Data_p8, Data_p9, Data_p10, Data_p11, mem_read
  BarrelShifter #(.Bits(32)) barrelshifter_1 (.in(Imms), .shift(6'b000010), .out(Imms_lt__lt_2));
  BitExtender #(.inputBits(16), .outputBits(32)) bitextender_1 (.in(Imm26[17:2]), .out(Imms));
  EEPROMDualPort #(.AddrBits(24), .Bits(32)) \Donnée  (
    .A(Data_p8), .Din(Data_p9), .str(Data_p10), .C(C), .ld(Data_p11), .D(Data_p7));
  // cmd cmd_1: pin names not known; wires that end beside it: Co, Imm26[7:2], Imm26[22:18], beq, bgtz, blez, bne, cns, d_m, ereg, jal, jr, ld, mem_8, mfhi, mflo, mx_1, Ns, Op_ual, mx_shamt, str
  and and_4 (and_4_out, bne, ~eq_0);  // And
  and and_5 (and_5_out, beq, eq_0);
  and and_6 (and_6_out, bgtz, ~lt__eq_0);  // And
  and and_7 (and_7_out, blez, lt__eq_0);
  or or_2 (mx_br, and_4_out, and_5_out, and_6_out, and_7_out);

  // Other names for the same wires on the sheet: ImmNs[15:0] = Imm26[17:2]; Nf[5:0] = Imm26[7:2];
  //   shamt[4:0] = Imm26[12:8]; num_rd[4:0] = Imm26[17:13]; num_rt[4:0] = Imm26[22:18]; num_rs[4:0] = Imm26[27:23];
  //   res_ual[31:0] = res

  // Notes on the sheet:
  //   C: Hz: 1000
  //   mips complet à compléter Novembre 2020
  //   contents of rom_1 (hex, n*v repeats v):
  //   f8fbbd27,404bfaf,4beaf,21f01d00,1800c227,21300200,10000524,110023c,4424,2e05100c,
  //   0,800c48f,4000224,c000000,21100000,21e81e00,404bf8f,4be8f,804bd27,a000224,c000000,
  //   0,481,3008018,1c00100c,1000821,fbff801c,ffff8018,a8af,fcffbd23,ffff083c,c0004ad,400bd23,
  //   a88f,800e003,e8ffbd27,1400beaf,21f01d00,1800c4af,1c00c5af,1800c28f,0,2100422c,4004014,
  //   0,1000224,32000104,0,800c0af,15000104,0,800c28f,1c00c38f,0,21106200,110033c,1800c48f,
  //   0,80200400,40006324,21208300,800c38f,0,21188300,6380,0,43a0,800c28f,0,1004224,800c2af,
  //   800c28f,0,400422c,e8ff4014,0,1800c28f,0,4004224,c00c2af,a000104,0,c00c28f,1c00c38f,
  //   0,21106200,40a0,c00c28f,0,1004224,c00c2af,c00c28f,0,400422c,f3ff4014,0,21100000,21e81e00,
  //   1400be8f,1800bd27,800e003,0,d8ffbd27,2400bfaf,2000beaf,21f01d00,2800c4af,2c00c5af,
  //   3000c6af,2800c28f,0,42150200,1f004230,1800c2af,2c00c28f,1800c38f,0,43ac,3000c58f,
  //   1800c48f,2300100c,0,21e81e00,2400bf8f,2000be8f,2800bd27,800e003,0,d8ffbd27,2400bfaf,
  //   2000beaf,21f01d00,2800c4af,2c00c5af,3000c6af,2800c28f,0,2140200,1f004230,1800c2af,
  //   2c00c28f,1800c38f,0,43ac,3000c58f,1800c48f,2300100c,0,21e81e00,2400bf8f,2000be8f,
  //   2800bd27,800e003,0,d8ffbd27,2400bfaf,2000beaf,21f01d00,2800c4af,2c00c5af,3000c6af,
  //   2800c28f,0,c2120200,1f004230,1800c2af,2c00c28f,1800c38f,0,43ac,3000c58f,1800c48f,
  //   2300100c,0,21e81e00,2400bf8f,2000be8f,2800bd27,800e003,0,e0ffbd27,1c00beaf,21f01d00,
  //   2000c4af,2400c5af,2000224,800c2af,c00c0af,2400c28f,30000324,43a0,2400c28f,0,1004224,
  //   78000324,43a0,1000c0af,54000104,0,2000c28f,0,2170200,1400c2af,1400c28f,0,a00422c,
  //   13004014,0,800c28f,0,1004324,800c3af,21180200,2400c28f,0,21104300,1400c38f,0,ff006330,
  //   37006324,ff006330,1e0300,31e0300,43a0,31000104,0,1400c28f,0,15004010,0,800c28f,0,
  //   1004324,800c3af,21180200,2400c28f,0,21104300,1400c38f,0,ff006330,30006324,ff006330,
  //   1e0300,31e0300,43a0,1000224,c00c2af,19000104,0,1400c28f,0,15004014,0,c00c38f,1000224,
  //   11006214,0,800c28f,0,1004324,800c3af,21180200,2400c28f,0,21104300,1400c38f,0,ff006330,
  //   30006324,ff006330,1e0300,31e0300,43a0,2000c28f,0,110200,2000c2af,1000c28f,0,1004224,
  //   1000c2af,1000c28f,0,8004228,a9ff4014,0,800c28f,2400c38f,0,21106200,40a0,0,21e81e00,
  //   1c00be8f,2000bd27,800e003,0,d8ffbd27,2400beaf,21f01d00,2800c4af,2c00c5af,800c0af,
  //   2800c28f,0,c00c2af,1000c0af,1800c0af,1400c0af,1c00c0af,e000104,0,800c28f,0,1004224,
  //   800c2af,2800c38f,a000224,1004014,d000000,1a006200,12000000,10100000,12100000,2800c2af,
  //   2800c28f,0,f0ff4014,0,800c28f,2c00c38f,0,21106200,40a0,c00c38f,a000224,1004014,d000000,
  //   1a006200,12000000,10100000,1000c2af,1000c28f,0,3f004104,0,2c00c28f,2d000324,43a0,
  //   1000224,1400c2af,800c28f,0,1004224,2c00c38f,0,21106200,40a0,31000104,0,800c28f,0,
  //   ffff4224,800c2af,1000c28f,0,2004104,0,23100200,1800c2af,110023c,40054324,1800c28f,
  //   0,21106200,4280,0,1c00c2af,800c38f,1400c28f,0,21106200,21180200,2c00c28f,0,21104300,
  //   1c00c38f,0,1e0300,31e0300,43a0,c00c38f,a000224,1004014,d000000,1a006200,12000000,
  //   10100000,12100000,c00c2af,c00c38f,a000224,1004014,d000000,1a006200,12000000,10100000,
  //   1000c2af,c00c28f,0,cdff4014,0,0,21e81e00,2400be8f,2800bd27,800e003,0,e0ffbd27,1c00bfaf,
  //   1800beaf,21f01d00,2000c4af,2400c5af,2800c6af,2000c28f,0,804230,c21b0200,1000224,b006214,
  //   0,2000c38f,ffff013c,2234,25106200,21180200,2400c28f,0,43ac,d000104,0,2000c28f,0,804230,
  //   c2130200,7004014,0,2000c28f,0,ffff4330,2400c28f,0,43ac,2400c28f,0,428c,2800c58f,21200200,
  //   2a01100c,0,0,21e81e00,1c00bf8f,1800be8f,2000bd27,800e003,0,e0ffbd27,1c00bfaf,1800beaf,
  //   21f01d00,2000c4af,2400c5af,2800c6af,2000c28f,0,804230,c21b0200,1000224,b006214,0,
  //   2000c38f,ffff013c,2234,25106200,21180200,2400c28f,0,43ac,d000104,0,2000c28f,0,804230,
  //   c2130200,7004014,0,2000c28f,0,ffff4330,2400c28f,0,43ac,2400c28f,0,428c,2800c58f,21200200,
  //   b400100c,0,0,21e81e00,1c00bf8f,1800be8f,2000bd27,800e003,0,e0ffbd27,1c00bfaf,1800beaf,
  //   21f01d00,2000c4af,2400c5af,2800c6af,2000c28f,0,ffff4330,2400c28f,0,43ac,2400c28f,
  //   0,428c,2800c58f,21200200,b400100c,0,0,21e81e00,1c00bf8f,1800be8f,2000bd27,800e003,
  //   0,e0ffbd27,1c00bfaf,1800beaf,21f01d00,2000c4af,2400c5af,2800c6af,2000c38f,ff03013c,
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  //   contents of Donnée (hex, n*v repeats v):
  //   6000424,600100c,21200200,1000224,c000000,ffff0010,1000224,a4af,fcffbd23,18008200,
  //   12100000,ffff8420,faff8010,fcffbd23,a48f,800e003,24300020,20202020,24617400,20202020,
  //   24763000,20202020,24763100,20202020,24613000,20202020,24613100,20202020,24613200,
  //   20202020,24613300,20202020,24743000,20202020,24743100,20202020,24743200,20202020,
  //   24743300,20202020,24743400,20202020,24743500,20202020,24743600,20202020,24743700,
  //   20202020,24733000,20202020,24733100,20202020,24733200,20202020,24733300,20202020,
  //   24733400,20202020,24733500,20202020,24733600,20202020,24733700,20202020,24743800,
  //   20202020,24743900,20202020,246b3000,20202020,246b3100,20202020,24677000,20202020,
  //   24737000,20202020,24667000,20202020,24726100,20202020,3f002020,20202020,3f002020,
  //   20202020,6a200020,20202020,6a616c20,202020,62657120,202020,626e6520,202020,626c657a,
  //   20002020,6267747a,20002020,61646469,20002020,61646469,75200020,736c7469,20002020,
  //   736c7469,75200020,616e6469,20002020,6f726920,202020,786f7269,20002020,6c756920,202020,
  //   6d666330,20002020,3f002020,20202020,3f002020,20202020,3f002020,20202020,3f002020,
  //   20202020,3f002020,20202020,3f002020,20202020,3f002020,20202020,3f002020,20202020,
  //   3f002020,20202020,3f002020,20202020,3f002020,20202020,3f002020,20202020,3f002020,
  //   20202020,3f002020,20202020,3f002020,20202020,6c622000,20202020,3f002020,20202020,
  //   3f002020,20202020,6c772000,20202020,6c627520,202020,6c687520,202020,3f002020,20202020,
  //   3f002020,20202020,73622000,20202020,73682000,20202020,3f002020,20202020,73772000,
  //   20202020,3f002020,20202020,3f002020,20202020,3f002020,20202020,3f002020,20202020,
  //   3f002020,20202020,3f002020,20202020,3f002020,20202020,3f002020,20202020,3f002020,
  //   20202020,3f002020,20202020,3f002020,20202020,3f002020,20202020,3f002020,20202020,
  //   3f002020,20202020,3f002020,20202020,3f002020,20202020,3f002020,20202020,3f002020,
  //   20202020,3f002020,20202020,3f002020,20202020,736c6c20,202020,3f002020,20202020,73726c20,
  //   202020,73726120,202020,736c6c76,20002020,3f002020,20202020,73726c76,20002020,73726176,
  //   20002020,6a722000,20202020,6a616c72,20002020,6d6f767a,20002020,6d6f766e,20002020,
  //   73797363,616c6c00,3f002020,20202020,3f002020,20202020,3f002020,20202020,6d666869,
  //   20002020,6d746869,20002020,6d666c6f,20002020,6d746c6f,20002020,3f002020,20202020,
  //   3f002020,20202020,3f002020,20202020,3f002020,20202020,6d756c74,20002020,6d756c74,
  //   75200020,64697620,202020,64697675,20002020,3f002020,20202020,3f002020,20202020,3f002020,
  //   20202020,3f002020,20202020,61646420,202020,61646475,20002020,73756220,202020,73756275,
  //   20002020,616e6420,202020,6f722000,20202020,786f7220,202020,6e6f7220,202020,3f002020,
  //   20202020,3f002020,20202020,736c7420,202020,736c7475,20002020,3f002020,20202020,3f002020,
  //   20202020,3f002020,20202020,3f002020,20202020,3f002020,20202020,3f002020,20202020,
  //   3f002020,20202020,3f002020,20202020,3f002020,20202020,3f002020,20202020,3f002020,
  //   20202020,3f002020,20202020,3f002020,20202020,3f002020,20202020,3f002020,20202020,
  //   3f002020,20202020,3f002020,20202020,3f002020,20202020,3f002020,20202020,3f002020,
  //   20202020,30313233,34353637,38394142,43444546,23496e73,74727563,74696f6e,20696e63,
  //   6f6e6e75,65002c00,20202020,20202800,20202020,20202900,20202020,20200a20,20202020,
  //   20200000
endmodule

/* Test case:
C 	cp 		res
0 	0x400000	0x7FFF0000
C 	0x400004	0x7FFFEFFC
C 	0x400008	0x20020000
C 	0x40000C	0x2
C 	0x400010	X
C 	0x400014	X
C 	0x400018	0x10010000 	#lb $a0,0($t0)
C 	0x40001C	0x48 		#blez $a0,fin
C 	0x400020	x		#jal putChar
C 	0x400030	0x7FFFEFFC	#sw $t0,0($sp)
C 	0x400034	0x7FFFEFF8	#addi $sp,$sp-4
C 	0x400038	0xFFFF0000	#lui $t0,0x1001
C 	0x40003C	0xFFFF000C	#sw $a0,0xC($t0)
C 	0x400040	0x7FFFEFFC	#addi $sp,$sp-4
C 	0x400044	0x7FFFEFFC	#lw $t0,0(sp)
C 	0x400048	0x400024	#jr $ra
C 	0x400024	0x10010001	#addi $t0,$t0,1
C 	0x400028	0x48		#bgtz $t0,boucle
C 	0x400018	0x10010001	#lb $a0,0($t0)
C 	0x40001C	0x65 		#blez $a0,fin


#.data
#	chaine : .ascii "Hello world"
#.text
#	lui $t0,0x7FFF
#	ori $sp,$t0,0xEFFC
#	lui $t0,0x2002
#	li  $t1,2
#	div $t0,$t1
#	mflo $t0
#boucle:
#	lb $a0,0($t0)
#	blez $a0,fin
#	jal putChar
#	addi $t0,$t0,1
#	bgtz $a0,boucle
#fin:
#	beq $0,$0,fin
	

#putChar:
#	sw $t0,0($sp)
#	addi $sp,$sp,-4
#	lui $t0,0xFFFF
#	sw $a0,0xC($t0)
#	addi $sp,$sp,4
#	lw $t0,0($sp)
#	jr $ra
*/
